# Fritzing sketch servo (saved by Fritzing 0.9.3b)
breadboards: 1

parts:
  元件1 = Adafruit T-Cobbler Plus [part_number="Adafruit #1989 and #2028"]
  J1 = Basic Servo
  元件2 = SRF05 Ultrasonic Rangefinder
  R1 = Resistor [tolerance=±5% resistance=2k package=THT]
  R2 = Resistor [tolerance=±5% resistance=1k package=THT]

nets:
  N1: 元件1.GPIO18, J1.pulse
  N2: 元件1.GPIO23, 元件2.Trig
  N3: 元件1.GPIO24, R1.Pin_1, R2.Pin_0
  GND: J1.gnd, 元件2.GND, R1.Pin_0
  VCC: J1.vcc, 元件2.VCC
  N4: 元件2.Echo, R2.Pin_1

notes:
  HC-SR04,計算參考網址
  https://www.modmypi.com/blog/hc-sr04-ultrasonic-range-sensor-on-the-raspberry-pi

custom parts:
  Adafruit T-Cobbler Plus: The Raspberry Pi has landed on the Maker World like a 40-GPIO pinned, quad-USB ported, credit card sized bomb of DIY joy. And while you can use most of our great Model B accessories by hooking up our downgrade cable, its probably a good time to upgrade your set up and accessorize using all of the 40 pins. That's why we now carry the Assembled Adafruit Pi T-Cobbler Plus - Breakout + Cable for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
