# Fritzing sketch lcd_rfid_buzzer (saved by Fritzing 0.9.3b)
breadboards: 1

parts:
  元件1 = Adafruit T-Cobbler Plus [part_number="Adafruit #1989 and #2028"]
  J1 = Piezo Speaker  # not connected
  元件2 = RFID-RC522-v3
  LCM1602_IIC1 = LCM1602 IIC [part_number="LCM1602 IIC" chip_label="LCM1602 IIC" package="DIP (Dual Inline) [THT]"]
  LCD2 = LCD screen

nets:
  +3.3V: 元件1.+3.3V, 元件2.3.3V
  N1: 元件1.SDA, LCM1602_IIC1.SDA
  N2: 元件1.SCL, LCM1602_IIC1.SCL
  GND: 元件1.GND, 元件2.RST, LCM1602_IIC1.GND
  N3: 元件1.MOSI, 元件2.MISO
  N4: 元件1.MISO, 元件2.IRQ
  N5: 元件1.SCLK, 元件2.GND
  +5V: 元件1.+5V, LCM1602_IIC1.VCC
  N6: 元件1.GPIO24, 元件2.SDA
  N7: 元件1.GPIO25, 元件2.SCK
  N8: 元件1.CE0, 元件2.MOSI
  VSS: LCM1602_IIC1.VSS, LCD2.VSS
  VDD: LCM1602_IIC1.VDD, LCD2.VDD
  N9: LCM1602_IIC1.V0, LCD2.V0
  N10: LCM1602_IIC1.RS, LCD2.RS
  N11: LCM1602_IIC1.RW, LCD2.R/W
  N12: LCM1602_IIC1.E, LCD2.E
  N13: LCM1602_IIC1.D0, LCD2.DB0
  N14: LCM1602_IIC1.D1, LCD2.DB1
  N15: LCM1602_IIC1.D2, LCD2.DB2
  N16: LCM1602_IIC1.D3, LCD2.DB3
  N17: LCM1602_IIC1.D4, LCD2.DB4
  N18: LCM1602_IIC1.D5, LCD2.DB5
  N19: LCM1602_IIC1.D6, LCD2.DB6
  N20: LCM1602_IIC1.D7, LCD2.DB7
  N21: LCM1602_IIC1.A, LCD2.LED+
  N22: LCM1602_IIC1.K, LCD2.LED-

notes:
  不用理會pin腳上的文字，依順序安裝

custom parts:
  Adafruit T-Cobbler Plus: The Raspberry Pi has landed on the Maker World like a 40-GPIO pinned, quad-USB ported, credit card sized bomb of DIY joy. And while you can use most of our great Model B accessories by hooking up our downgrade cable, its probably a good time to upgrade your set up and accessorize using all of the 40 pins. That's why we now carry the Assembled Adafruit Pi T-Cobbler Plus - Breakout + Cable for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
  RFID-RC522-v3: A simple China made RFID-RC522 Reader (6x4 cm); do check the pin labels, as this is a MFRC522 based clone.
  LCM1602 IIC: I2C-Module to use a 1602 or 2004 LCD on with the wire.h libory Serial LCD Modul
